// Logisim project lv10_alu.circ as structural Verilog: 6 circuits, main circuit adder1
module adder1 (
  input  a,
  input  b,
  input  cin,
  output R,
  output cout
);

  wire and_1_out, and_2_out, and_3_out, and_4_out, and_5_out, and_6_out, and_7_out, not_1_out, not_2_out,
       not_3_out, not_4_out, not_5_out, not_6_out;

  not not_1 (not_1_out, a);
  not not_2 (not_2_out, b);
  not not_3 (not_3_out, a);
  not not_4 (not_4_out, cin);
  not not_5 (not_5_out, b);
  not not_6 (not_6_out, cin);
  and and_1 (and_1_out, b, cin);
  and and_2 (and_2_out, a, cin);
  and and_3 (and_3_out, a, b);
  and and_4 (and_4_out, not_1_out, not_2_out, cin);
  and and_5 (and_5_out, not_3_out, b, not_4_out);
  and and_6 (and_6_out, a, not_5_out, not_6_out);
  and and_7 (and_7_out, a, b, cin);
  or or_1 (cout, and_1_out, and_2_out, and_3_out);
  or or_2 (R, and_4_out, and_5_out, and_6_out, and_7_out);
endmodule

module adder4 (
  input  cin,
  input  [3:0] a,
  input  [3:0] b,
  output [3:0] R,
  output cout
);

  wire adder1_1_cout, adder1_2_cout, adder1_3_cout;

  adder1 adder1_1 (.a(a[0]), .b(b[0]), .cin(cin), .R(R[0]), .cout(adder1_1_cout));
  adder1 adder1_2 (.a(a[1]), .b(b[1]), .cin(adder1_1_cout), .R(R[1]), .cout(adder1_2_cout));
  adder1 adder1_3 (.a(a[2]), .b(b[2]), .cin(adder1_2_cout), .R(R[2]), .cout(adder1_3_cout));
  adder1 adder1_4 (.a(a[3]), .b(b[3]), .cin(adder1_3_cout), .R(R[3]), .cout(cout));
endmodule

module addOrSub (
  input  addSub,
  input  [3:0] a,
  input  [3:0] b,
  output [3:0] R,
  output cout
);

  wire [3:0] xor_1_out;

  assign xor_1_out = b ^ {4{addSub}};  // XOR_Gate xor_1, 4 bits wide
  adder4 adder4_1 (.cin(addSub), .a(a), .b(xor_1_out), .R(R), .cout(cout));
endmodule

module aluLogic (
  input  [3:0] a,
  input  [3:0] b,
  input  [1:0] LS,
  output [3:0] out_4
);

  wire [3:0] and_1_out, not_1_out, or_1_out, xor_1_out;

  assign and_1_out = a & b;  // AND_Gate and_1, 4 bits wide
  assign or_1_out = a | b;  // OR_Gate or_1, 4 bits wide
  assign xor_1_out = a ^ b;  // XOR_Gate xor_1, 4 bits wide
  assign not_1_out = ~or_1_out;  // NOT_Gate not_1, 4 bits wide
  Multiplexer #(.select(2), .width(4), .enable("false")) multiplexer_1 (
    .in0(and_1_out), .in1(or_1_out), .in2(not_1_out), .in3(xor_1_out), .out(out_4), .sel(LS));
endmodule

module alu (
  input  [3:0] a,
  input  [3:0] b,
  input  [2:0] in_3,
  output [3:0] R
);

  wire aluops_1_o0, aluops_1_o3;
  wire [1:0] aluops_1_o1;
  wire [3:0] addorsub_1_r, alulogic_1_out_4;

  aluOps aluops_1 (
    .i0(in_3[0]), .i1(in_3[1]), .i2(in_3[2]), .o0(aluops_1_o0), .o1(aluops_1_o1[0]), .o2(aluops_1_o1[1]),
    .o3(aluops_1_o3));
  aluLogic alulogic_1 (.a(a), .b(b), .LS(aluops_1_o1), .out_4(alulogic_1_out_4));
  addOrSub addorsub_1 (.addSub(aluops_1_o0), .a(a), .b(b), .R(addorsub_1_r));  // open: cout
  Multiplexer #(.width(4), .enable("false")) multiplexer_1 (
    .in0(addorsub_1_r), .in1(alulogic_1_out_4), .out(R), .sel(aluops_1_o3));
endmodule

module aluOps (
  input  i0,
  input  i1,
  input  i2,
  output o0,
  output o1,
  output o2,
  output o3
);

  not not_1 (o1, i1);
  or or_1 (o3, i1, i0);

  assign o0 = i2;
  assign o2 = i2;
endmodule
