// Logisim project lv10_cpu.circ as structural Verilog: 6 circuits, main circuit main
module main (
  input  in_1,
  input  in_2
);

  wire clock_1_out, maincontrol_1_alusrc, maincontrol_1_extop, maincontrol_1_memread, maincontrol_1_memtoreg,
       maincontrol_1_memwrite, maincontrol_1_regdst, maincontrol_1_regwrite, registerfile_1_p6;
  wire [3:0] mips_alu_1_p3;
  wire [4:0] mipsprogramrom_1_p1_2, multiplexer_1_out;
  wire [31:0] extender_1_out_3, incrementer_1_p3, mips_alu_1_p5, mips_ram_1_p6, mipsprogramrom_1_p1,
       mipsprogramrom_1_p3, multiplexer_2_out, registerfile_1_p7;
  wire [31:2] incrementer_1_p1;

  // Incrementer #(.width(30)) incrementer_1: pin names not known; wires that end beside it: incrementer_1_p1, incrementer_1_p3[31:2], {incrementer_1_p1, incrementer_1_p3[1:0]}
  Clock clock_1 (.out(clock_1_out));
  Register #(.width(32)) register_1 (
    .D(incrementer_1_p3), .en(in_1), .clk(clock_1_out), .Q({incrementer_1_p1, incrementer_1_p3[1:0]}),
    .clr(in_2));
  // MIPSProgramROM mipsprogramrom_1: pin names not known; wires that end beside it: {mipsprogramrom_1_p1[31:11], mipsprogramrom_1_p1_2, mipsprogramrom_1_p1[5:0]}, {mipsprogramrom_1_p1[15:11], mipsprogramrom_1_p1_2, mipsprogramrom_1_p1[5:0]}, mipsprogramrom_1_p3
  Multiplexer #(.width(5), .enable("false")) multiplexer_1 (
    .in0(mipsprogramrom_1_p1[20:16]), .in1(mipsprogramrom_1_p1[15:11]), .out(multiplexer_1_out),
    .sel(maincontrol_1_regdst));
  mainControl maincontrol_1 (
    .in_1(mipsprogramrom_1_p1[31:26]), .RegDst(maincontrol_1_regdst), .RegWrite(maincontrol_1_regwrite),
    .ExtOp(maincontrol_1_extop), .ALUSrc(maincontrol_1_alusrc), .MemRead(maincontrol_1_memread),
    .MemWrite(maincontrol_1_memwrite), .MemtoReg(maincontrol_1_memtoreg));  // open: Beq, Bne, J
  // RegisterFile registerfile_1: pin names not known; wires that end beside it: clock_1_out, maincontrol_1_regwrite, multiplexer_1_out, mipsprogramrom_1_p1[25:21], mipsprogramrom_1_p1[20:16], registerfile_1_p6, registerfile_1_p7
  Multiplexer #(.width(32), .enable("false")) multiplexer_2 (
    .in0(registerfile_1_p7), .in1(extender_1_out_3), .out(multiplexer_2_out), .sel(maincontrol_1_alusrc));
  extender extender_1 (
    .Immediate({mipsprogramrom_1_p1[15:11], mipsprogramrom_1_p1_2, mipsprogramrom_1_p1[5:0]}),
    .ExtOp(maincontrol_1_extop), .out_3(extender_1_out_3));
  // Mips_ALU mips_alu_1: pin names not known; wires that end beside it: registerfile_1_p6, multiplexer_2_out, mips_alu_1_p3, mipsprogramrom_1_p1_2, mips_alu_1_p5
  ALUcontrol alucontrol_1 (
    .funct(mipsprogramrom_1_p1[5:0]), .opcode(mipsprogramrom_1_p1[31:26]), .AluOP(mips_alu_1_p3));
  // MIPS_RAM #(.addrWidth(24)) mips_ram_1: pin names not known; wires that end beside it: mips_alu_1_p5[23:0], registerfile_1_p7, maincontrol_1_memwrite, clock_1_out, maincontrol_1_memread, mips_ram_1_p6
  Multiplexer #(.width(32), .enable("false")) multiplexer_3 (
    .in0(mips_alu_1_p5), .in1(mips_ram_1_p6), .out(mipsprogramrom_1_p3), .sel(maincontrol_1_memtoreg));

  // Notes on the sheet:
  //   contents of mipsprogramrom_1 (hex, n*v repeats v):
  //   addiu $t1, $0, 0xA or $t2, $t0, $t1 sll $t3, $t2, 3 sw $t3, 0($0) lw $t4, 0($0)
endmodule

module extender (
  input  [15:0] Immediate,
  input  ExtOp,
  output [31:0] out_3
);

  wire [31:0] bit_extender_1_out, bit_extender_2_out;

  assign bit_extender_1_out = {{16{1'b0}}, Immediate};  // Bit_Extender bit_extender_1
  assign bit_extender_2_out = {{16{Immediate[15]}}, Immediate};  // Bit_Extender bit_extender_2
  Multiplexer #(.width(32), .enable("false")) multiplexer_1 (
    .in0(bit_extender_1_out), .in1(bit_extender_2_out), .out(out_3), .sel(ExtOp));
endmodule

module mainControl (
  input  [5:0] in_1,
  output RegDst,
  output RegWrite,
  output ExtOp,
  output ALUSrc,
  output Beq,
  output Bne,
  output J,
  output MemRead,
  output MemWrite,
  output MemtoReg
);

  wire and_1_out, and_2_out, and_3_out, not_1_out, not_2_out, not_3_out, not_4_out, not_5_out, not_6_out,
       not_7_out, not_8_out, not_9_out, not_10_out, not_12_out, not_13_out, not_14_out, not_15_out,
       not_16_out, not_17_out, not_18_out;

  not not_1 (not_1_out, in_1[5]);
  not not_2 (not_2_out, in_1[4]);
  not not_3 (not_3_out, in_1[3]);
  not not_4 (not_4_out, in_1[2]);
  not not_5 (not_5_out, in_1[1]);
  not not_6 (not_6_out, in_1[0]);
  not not_7 (not_7_out, in_1[2]);
  not not_8 (not_8_out, in_1[1]);
  not not_9 (not_9_out, in_1[5]);
  not not_10 (not_10_out, in_1[3]);
  not not_11 (ExtOp, in_1[2]);
  not not_12 (not_12_out, in_1[3]);
  not not_13 (not_13_out, in_1[0]);
  not not_14 (not_14_out, in_1[3]);
  not not_15 (not_15_out, in_1[1]);
  not not_16 (not_16_out, in_1[3]);
  not not_17 (not_17_out, in_1[0]);
  not not_18 (not_18_out, in_1[3]);
  and and_1 (and_1_out, not_7_out, not_8_out);
  and and_2 (and_2_out, not_9_out, in_1[3]);
  and and_3 (and_3_out, in_1[5], not_10_out);
  or or_1 (ALUSrc, in_1[1], in_1[3]);
  and and_4 (Beq, not_12_out, in_1[2], not_13_out);
  and and_5 (Bne, not_14_out, not_15_out, in_1[0]);
  and and_6 (J, not_16_out, in_1[1], not_17_out);
  and and_7 (MemRead, in_1[5], not_18_out);
  and and_8 (MemWrite, in_1[5], in_1[3]);
  and and_9 (RegDst, not_1_out, not_2_out, not_3_out, not_4_out, not_5_out, not_6_out);
  or or_2 (RegWrite, and_1_out, and_2_out, and_3_out);

  assign MemtoReg = in_1[5];
endmodule

module ALURtip (
  input  [5:0] in_1,
  output o4,
  output o3,
  output o2,
  output o1
);

  wire and_1_out, and_2_out, not_1_out, not_2_out, not_3_out;

  not not_1 (not_1_out, in_1[1]);
  not not_2 (not_2_out, in_1[2]);
  not not_3 (not_3_out, in_1[5]);
  and and_1 (and_1_out, not_1_out, in_1[0]);
  and and_2 (and_2_out, in_1[5], not_2_out);
  and and_3 (o1, not_3_out, in_1[0]);
  or or_1 (o2, and_1_out, and_2_out);

  assign o3 = in_1[1];
  assign o4 = in_1[2];
endmodule

module ALUItip (
  input  [5:0] in_1,
  output o4,
  output o3,
  output o2,
  output o1
);

  wire and_2_out, and_3_out, not_1_out, not_2_out, not_3_out, not_4_out, not_5_out;

  and and_1 (o4, in_1[3], in_1[2]);
  not not_1 (not_1_out, in_1[3]);
  not not_2 (not_2_out, in_1[1]);
  not not_3 (not_3_out, in_1[0]);
  not not_4 (not_4_out, in_1[3]);
  not not_5 (not_5_out, in_1[2]);
  and and_2 (and_2_out, not_1_out, not_2_out);
  and and_3 (and_3_out, in_1[1], not_3_out);
  or or_1 (o2, not_4_out, not_5_out, in_1[0]);
  or or_2 (o3, and_2_out, and_3_out);

  assign o1 = 1'b0;
endmodule

module ALUcontrol (
  input  [5:0] funct,
  input  [5:0] opcode,
  output [3:0] AluOP
);

  wire nor_1_out;
  wire [3:0] aluitip_1_o1, alurtip_1_o1;

  ALURtip alurtip_1 (
    .in_1(funct), .o4(alurtip_1_o1[3]), .o3(alurtip_1_o1[2]), .o2(alurtip_1_o1[1]), .o1(alurtip_1_o1[0]));
  ALUItip aluitip_1 (
    .in_1(opcode), .o4(aluitip_1_o1[3]), .o3(aluitip_1_o1[2]), .o2(aluitip_1_o1[1]), .o1(aluitip_1_o1[0]));
  nor nor_1 (nor_1_out, opcode[0], opcode[1], opcode[2], opcode[3], opcode[4], opcode[5]);
  Multiplexer #(.width(4), .enable("false")) multiplexer_1 (
    .in0(aluitip_1_o1), .in1(alurtip_1_o1), .out(AluOP), .sel(nor_1_out));
endmodule
